# Fritzing sketch rpiled-24-1f (saved by Fritzing 0.8.3b)
circuit board: 4.96156cm x 2.92375cm
breadboards: 1

parts:
  GRN = STP16NF06 N-Channel Power MOSFET
  BLU = STP16NF06 N-Channel Power MOSFET
  RED = STP16NF06 N-Channel Power MOSFET
  RGBO = female pin header, 4 pins [form="♀ (female)"]
  RGB = female pin header, 3 pins [form="♀ (female)"]
  RPi = Adafruit Pi Cobbler
  PWM = female pin header, 6 pins [form="♀ (female)"]
  V+ = female pin header, 3 pins [form="♀ (female)"]
  R+ = Resistor [tolerance=±5% resistance=1k package=THT]
  G+ = Resistor [tolerance=±5% resistance=1k package=THT]
  B+ = Resistor [tolerance=±5% resistance=1k package=THT]
  B++ = Resistor [tolerance=±5% resistance=1k package=THT]
  G++ = Resistor [tolerance=±5% resistance=1k package=THT]
  R+_2 = Resistor [tolerance=±5% resistance=1k package=THT]
  PWR = female pin header, 2 pins [form="♀ (female)"]
  B1 = NPN-Transistor [package="TO92 [THT]"]
  G1 = NPN-Transistor [package="TO92 [THT]"]
  R1 = NPN-Transistor [package="TO92 [THT]"]

nets:
  N1: GRN.gate, RGB.pin2, G+.Pin_1
  N2: GRN.drain, G++.Pin_1, G1.E
  N3: GRN.source, BLU.source, RED.source, RPi.PIN20, PWR.pin2, B1.C, G1.C, R1.C
  N4: BLU.gate, RGB.pin3, B+.Pin_1
  N5: BLU.drain, B++.Pin_1, B1.E
  N6: RED.gate, RGB.pin1, R+.Pin_1
  N7: RED.drain, R+_2.Pin_1, R1.E
  N8: RGBO.pin1, PWR.pin1
  N9: RGBO.pin2, G1.B
  N10: RGBO.pin3, R1.B
  N11: RGBO.pin4, B1.B
  N12: RPi.3V3, PWM.pin1
  N13: RPi.GND, PWM.pin2
  N14: RPi.MOSI, PWM.pin3
  N15: RPi.SCLK, PWM.pin4
  N16: RPi.CE0, PWM.pin6
  N17: V+.pin1, R+.Pin_0, R+_2.Pin_0
  N18: V+.pin2, G+.Pin_0, G++.Pin_0
  N19: V+.pin3, B+.Pin_0, B++.Pin_0

notes:
  These pinheaders are for the AdaFruit 24-channel 12-bit PWM (ID: 1429).
  12V
  This is the pinheader for the LED RGB flexistrip.
  NOTE: The MOSFET releases the Source when the Gate is HIGH. However, the 1429 turns the LEDs on when the voltage is LOW. A second set of MOSFETs corrects the inversion and smooths fading.
  Source: http://forums.adafruit.com/viewtopic.php?p=218857#p218857

custom parts:
  STP16NF06 N-Channel Power MOSFET: STP16NF06 N-channel Power MOSFET
  Adafruit Pi Cobbler: Adafruit Pi Cobbler GPIO Breakout for Raspberry Pi
